# Fritzing sketch tester (saved by Fritzing 0.9.3b)
breadboards: 1

parts:
  Componente1 = Arduino Uno (Rev3)
  R1 = Trimmer Potentiometer [maximum_resistance=10kΩ package=THT]
  LCD1 = LCD screen
  R2 = Resistor [tolerance=±5% resistance=220 package=THT]
  R3 = Resistor [tolerance=±5% resistance=220 package=THT]
  R4 = Resistor [tolerance=±5% resistance=220 package=THT]
  R5 = Resistor [tolerance=±5% resistance=220 package=THT]
  D1 = LTE-302 [package=lte-302]
  D2 = LTE-302 [package=lte-302]
  D3 = LTE-302 [package=lte-302]

nets:
  N1: Componente1.A0, R2.Pin_0
  N2: Componente1.D8, LCD1.E
  N3: Componente1.D9_PWM, LCD1.DB4
  N4: Componente1.D10_PWM/SS, LCD1.DB5
  N5: Componente1.D11_PWM/MOSI, LCD1.DB6
  N6: Componente1.D12/MISO, LCD1.DB7
  GND: Componente1.GND, R1.leg2, LCD1.VSS, LCD1.R/W, LCD1.LED-, R2.Pin_1, R3.Pin_1, R4.Pin_1
  N7: Componente1.D7, LCD1.RS
  5V: Componente1.5V, R1.leg1, LCD1.VDD, LCD1.LED+
  N8: R1.wiper, LCD1.V0
  N9: R3.Pin_0, D1.C
  N10: R4.Pin_0, D2.C
  N11: R5.Pin_0, D3.C

notes:
  10KO
  220O
  Puntas donde se conecta la bateria
